# Fritzing sketch HitagiExpansionBoard (saved by Fritzing 0.9.5d)
circuit board: 10.5cm x 13.5033cm
breadboards: 1

parts:
  SparkFun_Pro_Micro_5v = SparkFun Pro Micro [part_number=DEV-12640]
  STEMMA = female pin header, 4 pins [form="♀ (female)"]
  BAT1 = BC9VPC [package=bc9vpc]
  POWER = Toggle Switch [package=THT]
  STEMMA1 = Adafruit Stemma 4 pin header [form="♀ (female)" package=THT]
  PWM(6) = female pin header, 3 pins [form="♀ (female)"]
  Part1 = TFT 2.2 inch 320x240 w microSD [part_number=1480]
  R8 = Resistor [tolerance=±5% resistance=330 package="0805 [SMD]"]
  Pin10 = LED - 5mm [color="Red (633nm)" package="5 mm [THT]"]
  RESET = Pushbutton [package="[SMD]"]
  SPI1 = JST PH SPI HEADER [form="♀ (female)" package=THT]
  PWM(5) = female pin header, 3 pins [form="♀ (female)"]
  D4/A6 = female pin header, 3 pins [form="♀ (female)"]
  Pin9 = LED - 5mm [color="Red (633nm)" package="5 mm [THT]"]
  R9 = Resistor [tolerance=±5% resistance=330 package="0805 [SMD]"]
  SPI0 = JST PH SPI HEADER [form="♀ (female)" package=THT]

nets:
  9V: SparkFun_Pro_Micro_5v.RAW, POWER.COM
  GND: SparkFun_Pro_Micro_5v.GND, STEMMA.pin1, BAT1.V-, STEMMA1.GND, PWM(6).pin1, Part1.GND, Pin10.cathode, RESET.Pin_3, RESET.Pin_4, SPI1.GND, PWM(5).pin1, D4/A6.pin1, Pin9.cathode, SPI0.GND
  RESET: SparkFun_Pro_Micro_5v.RESET, RESET.Pin_1, RESET.Pin_2
  5V: SparkFun_Pro_Micro_5v.VCC, STEMMA.pin2, STEMMA1.V+, PWM(6).pin2, Part1.VIN, SPI1.VCC, PWM(5).pin2, D4/A6.pin2, SPI0.VCC
  SPI1 Enable: SparkFun_Pro_Micro_5v.A3, SPI1.CS_
  SPI0 Enable: SparkFun_Pro_Micro_5v.A2, SPI0.CS_
  SDCS: SparkFun_Pro_Micro_5v.A1, Part1.SDCS
  LCD Enable: SparkFun_Pro_Micro_5v.A0, Part1.LCDCS
  SCK: SparkFun_Pro_Micro_5v.SCK, Part1.SCLK, SPI1.SCK, SPI0.SCK
  MISO: SparkFun_Pro_Micro_5v.MISO, Part1.MISO, SPI1.MISO, SPI0.MISO
  MOSI: SparkFun_Pro_Micro_5v.MOSI, Part1.MOSI, SPI1.MOSI, SPI0.MOSI
  LED0: SparkFun_Pro_Micro_5v.D10, R8.Pin_0
  LED1: SparkFun_Pro_Micro_5v.D9, R9.Pin_0
  LCD RESET: SparkFun_Pro_Micro_5v.D8, Part1.RESET
  DC: SparkFun_Pro_Micro_5v.D7, Part1.DC
  PWM0: SparkFun_Pro_Micro_5v.D6, PWM(6).pin3
  PWM1: SparkFun_Pro_Micro_5v.D5, PWM(5).pin3
  D4: SparkFun_Pro_Micro_5v.D4, D4/A6.pin3
  SCL: SparkFun_Pro_Micro_5v.D3, STEMMA.pin4, STEMMA1.SCL
  SDA: SparkFun_Pro_Micro_5v.D2, STEMMA.pin3, STEMMA1.SDA
  9V IN: BAT1.V+, POWER.L1
  N1: R8.Pin_1, Pin10.anode
  N2: Pin9.anode, R9.Pin_1

notes:
  REV 4
  "Hitagi" Expansion Board
  (C) 2020 Joshua Scoggins

custom parts:
  SparkFun Pro Micro: This tiny little board does all of the neat-o Arduino tricks that you’re familiar with: 4 channels of 10-bit ADC, 5 PWM pins, 12 DIOs as well as hardware serial connections Rx and Tx. Running at 16MHz and 5V, this board will remind you a lot of your other favorite Arduino-compatible boards but this little guy can go just about anywhere. There is a voltage regulator on board so it can accept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
  Adafruit Stemma 4 pin header: Adafruit STEMMA 4 pin header JST PH 4
  TFT 2.2 inch 320x240 w microSD: This lovely little display breakout is the best way to add a small, colorful and bright display to any project. Since the display uses 4-wire SPI to communicate and has its own pixel-addressable frame buffer, it can be used with every kind of microcontroller. Even a very small one with low memory and few pins available! The 2.2" display has 320x240 color pixels.
  JST PH SPI HEADER: Single device JST PH Based SPI Header
